# Fritzing sketch BeeBot (saved by Fritzing 0.9.6b)
breadboards: 2

parts:
  Uno = Arduino Uno (Rev3)
  S1 = Pushbutton [package="[THT]"]
  S2 = Pushbutton [package="[THT]"]
  S3 = Pushbutton [package="[THT]"]
  Q1 = NPN-Transistor [package="TO92 [THT]"]
  Q2 = NPN-Transistor [package="TO92 [THT]"]
  D1 = Rectifier Diode [part_number=1N4001 package="300 mil [THT]"]
  D2 = Rectifier Diode [part_number=1N4001 package="300 mil [THT]"]
  R1 = Resistor [tolerance=±5% power=0.25 resistance=330 package=THT]
  R2 = Resistor [tolerance=±5% power=0.25 resistance=330 package=THT]
  R3 = Resistor [tolerance=±5% power=0.25 resistance=10k package=THT]
  R4 = Resistor [tolerance=±5% power=0.25 resistance=10k package=THT]
  R5 = Resistor [tolerance=±5% power=0.25 resistance=10k package=THT]
  Left_Motor = gear-motor
  Right_Motor = gear-motor
  HC-SR04_Sensor = HC-SR04 Ultrasonic Distance Sensor

nets:
  N1: Uno.D9_PWM, HC-SR04_Sensor.ECHO
  N2: Uno.D10_PWM/SS, HC-SR04_Sensor.TRIG
  GND: Uno.GND, Q1.E, Q2.E, R3.Pin_1, R4.Pin_1, R5.Pin_1, HC-SR04_Sensor.GND
  N3: Uno.D2, S1.Pin_1, S1.Pin_2, R5.Pin_0
  N4: Uno.D3_PWM, S2.Pin_1, S2.Pin_2, R4.Pin_0
  N5: Uno.D4, S3.Pin_1, S3.Pin_2, R3.Pin_0
  N6: Uno.D5_PWM, R2.Pin_1
  N7: Uno.D6_PWM, R1.Pin_1
  5V: Uno.5V, S1.Pin_3, S1.Pin_4, S2.Pin_3, S2.Pin_4, S3.Pin_3, S3.Pin_4, D1.cathode, D2.cathode, Left_Motor.pin_2, Right_Motor.pin_2, HC-SR04_Sensor.VCC
  N8: Q1.B, R1.Pin_0
  N9: Q1.C, D1.anode, Left_Motor.pin_1
  N10: Q2.B, R2.Pin_0
  N11: Q2.C, D2.anode, Right_Motor.pin_1
